# Fritzing sketch Drink Lantern (saved by Fritzing 0.8.7b)
circuit board: 3.0601cm x 4.07162cm
breadboards: 1

parts:
  R1 = Resistor [tolerance=±5% resistance=100k package=THT]
  R2 = Resistor [tolerance=±5% resistance=3.3 package=THT]
  LED1 = LED - 5mm [color="White (6500K)" part_number="Adafruit PID 518" package="5 mm [THT]"]
  Q3 = NPN-Transistor [part_number="Adafruit PID756" package="TO92 [THT]"]
  S1 = Pushbutton [package="[THT]"]
  VCC1 = Battery
  Q2 = Basic FET N-Channel [part_number="Adafruit PID 355" package="TO220 [THT]"]

nets:
  N1: R1.Pin_0, LED1.anode, VCC1.+
  N2: R1.Pin_1, Q3.C, Q2.gate
  N3: R2.Pin_0, Q3.B, Q2.source
  N4: R2.Pin_1, Q3.E, S1.Pin_1, S1.Pin_2
  N5: LED1.cathode, Q2.drain
  N6: S1.Pin_3, S1.Pin_4, VCC1.-
